# Fritzing sketch temp_monitor_zvpA1LFzWa (saved by Fritzing 0.9.3b)
breadboards: 1

parts:
  U1 = NodeMCU V1.0
  R1 = Resistor [tolerance=±5% resistance=4.7k package=THT]
  DS1 = DS18B20 1-Wire Temperature Sensor [part_number=DS18B20]

nets:
  N1: U1.D4, R1.Pin_1, DS1.DQ
  3V3: U1.3V3, R1.Pin_0, DS1.VDD
  GND: U1.GND, DS1.GND

custom parts:
  NodeMCU V1.0: ESP8266 based NodeMCU
